# Fritzing sketch KSSR22 (saved by Fritzing 0.9.2b)
breadboards: 1

parts:
  Part1 = Arduino Uno (Rev3)
  Part2 = Logic Level Converter
  Power_plug1 = Power plug  # not connected
  U1 = ESP8266 WiFi Module [part_number=ESP8266]
  Grove1 = Grove Buzz
  LED1 = LED - 5mm [color="Red (633nm)" package="5 mm [THT]"]
  R1 = Resistor [tolerance=±5% resistance=100k package=THT]

nets:
  N1: Part1.A0, Grove1.SIG
  N2: Part1.D12/MISO, R1.Pin_0
  N3: Part1.D0/RX, Part2.TX_HV
  N4: Part1.D1/TX, Part2.RX_HV
  3V3: Part1.3V3, Part2.LV, U1.VCC
  5V: Part1.5V, Part2.HV, Grove1.VCC
  GND: Part1.GND, Part2.GND, U1.GND, Grove1.GND, LED1.cathode
  N5: Part2.RX_LV, U1.RXD
  N6: Part2.TX_LV, U1.TXD
  N7: LED1.anode, R1.Pin_1

custom parts:
  ESP8266 WiFi Module: Generic WiFi Module based on the ESP8266 with onboard PCB antenna and UART communications
